// Logisim project Combined.circ as structural Verilog: 1 circuit, main circuit main
module main (
  input  in_1,
  output [6:0] out_2,
  output out_3,
  output [31:0] out_4,
  output [31:0] out_5,
  output [31:0] out_6,
  output [31:0] out_7,
  output [31:0] out_8,
  output out_9,
  output [31:0] out_10,
  output [1:0] out_11,
  output [31:0] out_12,
  output out_13,
  output [3:0] out_14,
  output [31:0] out_15,
  output [31:0] out_16,
  output [2:0] out_17,
  output [31:0] out_18
);

  wire main_1_p3, main_2_p2, main_2_p3, main_2_p5, main_2_p7, main_2_p11, main_2_p12;
  wire [1:0] main_2_p8;
  wire [31:0] main_1_p6, main_1_p7, main_3_p4, main_3_p6, multiplexer_2_out, multiplexer_3_out,
       multiplexer_4_out, ram_1_data;

  Multiplexer #(.select(2), .width(32), .enable("false")) multiplexer_1 (
    .in0(out_10), .in1(main_1_p6), .in2(main_1_p7), .in3(out_5), .out(out_6), .sel(out_11));
  Register #(.width(32)) PC (.D(out_6), .Q(out_7), .clk(out_13), .clr(in_1));  // open: en
  Clock clock_1 (.out(out_13));
  Adder #(.width(32)) adder_1 (.a(out_7), .b(32'h4), .out(out_10));  // open: cin, cout
  ROM #(.addrWidth(10), .dataWidth(32)) rom_1 (.addr(out_7[11:2]), .data({out_8[31:7], out_2}));  // open: sel
  // immediate_block_main main_1: pin names not known; wires that end beside it: out_7, {out_8[31:7], out_2}, main_1_p3, out_13, out_16, main_1_p6, main_1_p7, in_1
  // Completed_Controller_main main_2: pin names not known; wires that end beside it: out_2, main_2_p2, main_2_p3, out_9, main_2_p5, out_3, main_2_p7, main_2_p8, main_1_p3, out_11, main_2_p11, main_2_p12
  // Register_Files_Block_main main_3: pin names not known; wires that end beside it: out_8[19:15], out_8[24:20], out_8[11:7], main_3_p4, main_2_p7, main_3_p6, out_4
  Multiplexer #(.select(2), .width(32), .enable("false")) multiplexer_2 (
    .in0(main_3_p6), .in1(out_10), .in2(out_7), .out(multiplexer_2_out), .sel(main_2_p8));  // open: in3
  Multiplexer #(.width(32), .enable("false")) multiplexer_3 (
    .in0(out_4), .in1(out_16), .out(multiplexer_3_out), .sel(main_2_p3));
  // ALU_Branch_Controller_main main_4: pin names not known; wires that end beside it: main_3_p6, out_4, out_8[14:12], main_2_p2
  // ALU_COntroller alu_controller_1: pin names not known; wires that end beside it: out_8[30], out_8[14:12], main_2_p12, out_14, out_5, out_15
  // ALU_Circuit_main main_5: pin names not known; wires that end beside it: multiplexer_2_out, multiplexer_3_out, out_14, out_5
  RAM #(.addrWidth(10), .dataWidth(32), .bus("separate")) ram_1 (
    .addr(out_5[11:2]), .din(out_4), .data(ram_1_data), .str(out_9), .clk(out_13), .ld(main_2_p5), .clr(in_1));  // open: sel
  Multiplexer #(.width(32), .enable("false")) multiplexer_4 (
    .in0(out_5), .in1(ram_1_data), .out(multiplexer_4_out), .sel(out_3));
  Multiplexer #(.width(32), .enable("false")) multiplexer_5 (
    .in0(multiplexer_4_out), .in1(out_10), .out(main_3_p4), .sel(main_2_p11));

  assign out_8[6:0] = out_2;
  assign out_12 = out_6;
  assign out_17 = out_8[14:12];
  assign out_18 = out_7;

  // Notes on the sheet:
  //   contents of rom_1 (hex, n*v repeats v):
  //   40006f 3f500613 c2a023 128683
  //   rd
endmodule
