// Logisim project CPU Stages.circ as structural Verilog: 1 circuit, main circuit main
module main (
  input  Reset,
  output [31:0] Output
);

  wire clock_1_out;
  wire [9:0] Program_Counter_q;
  wire [31:0] adder_1_out;
  wire [31:10] Program_Counter_q_2;

  Clock clock_1 (.out(clock_1_out));
  Adder #(.width(32)) adder_1 (
    .a(32'h4), .b({Program_Counter_q_2, Program_Counter_q}), .out(adder_1_out));  // open: cin, cout
  Register #(.width(32)) Program_Counter (
    .D(adder_1_out), .Q({Program_Counter_q_2, Program_Counter_q}), .clk(clock_1_out), .clr(Reset));  // open: en
  ROM #(.addrWidth(10), .dataWidth(32)) rom_1 (.addr(Program_Counter_q), .data(Output));  // open: sel
endmodule
